# Fritzing sketch flip flop (saved by Fritzing 0.9.1b)
breadboards: 1

parts:
  Part1 = Arduino Uno (Rev3)
  LED1 = LED - 5mm [color="Red (633nm)" package="5 mm [THT]"]
  R1 = Resistor [tolerance=±5% resistance=220 package=THT]
  LED2 = LED - 5mm [color="Yellow (595nm)" package="5 mm [THT]"]
  R2 = Resistor [tolerance=±5% resistance=220 package=THT]

nets:
  N1: Part1.D10_PWM/SS, R2.Pin_1
  N2: Part1.D11_PWM/MOSI, R1.Pin_1
  N3: Part1.GND, LED1.cathode, LED2.cathode
  N4: LED1.anode, R1.Pin_0
  N5: LED2.anode, R2.Pin_0

// code stored in the sketch: Untitled.ino
int ledPin1 = 10;
int ledPin2 = 11;

void setup() {
	pinMode(ledPin1, OUTPUT);
	pinMode(ledPin2, OUTPUT);
}

void loop() {
	digitalWrite(ledPin1, HIGH);
	digitalWrite(ledPin2, LOW);
	delay(300);
	digitalWrite(ledPin1, LOW);
	digitalWrite(ledPin2, HIGH);
	delay(300);	
}
