# Fritzing sketch traffic light (saved by Fritzing 0.9.1b)
breadboards: 1

parts:
  Part1 = Arduino Uno (Rev3)
  R1 = Resistor [tolerance=±5% resistance=220 package=THT]
  R2 = Resistor [tolerance=±5% resistance=220 package=THT]
  LED1 = LED - 3mm [color="Red (633nm)" package="3 mm [THT]"]  # not connected
  LED2 = LED - 3mm [color="Yellow (592nm)" package="3 mm [THT]"]  # not connected
  LED3 = LED - 3mm [color="Green (555nm)" package="3 mm [THT]"]
  R3 = Resistor [tolerance=±5% resistance=220 package=THT]

nets:
  N1: Part1.D9_PWM, R3.Pin_1
  N2: Part1.D10_PWM/SS, R2.Pin_1
  N3: Part1.D11_PWM/MOSI, R1.Pin_1
  N4: Part1.GND, LED3.cathode
  N5: LED3.anode, R3.Pin_0

// code stored in the sketch: Untitled.ino
int ledPinGreen = 9;
int ledPinYellow = 10;
int ledPinRed = 11;

void setup() {
	pinMode(ledPinGreen, OUTPUT);
	pinMode(ledPinYellow, OUTPUT);
	pinMode(ledPinRed, OUTPUT);
}

void loop() {
	//dega raudona 5 sekundes
	digitalWrite(ledPinRed, HIGH);
	digitalWrite(ledPinYellow, LOW);
	digitalWrite(ledPinGreen, LOW);
	delay(5000);

	//kartu uzsidega geltona 1 sekundei
	digitalWrite(ledPinYellow, HIGH);
	delay(1000);

	//dega zalia 5 sekundes
	digitalWrite(ledPinRed, LOW);
	digitalWrite(ledPinYellow, LOW);
	digitalWrite(ledPinGreen, HIGH);
	delay(5000);

	//mirksi zalia tris kartus kas puse sekundes
	for (int i=1; i<=4; i++) {
		if (i mod 2 == 1) {
			digitalWrite(ledPinGreen, LOW);		
		} else
			digitalWrite(ledPinGreen, HIGH);
		delay(500);
	}

	//uzsidega geltona 1 sekundei
	digitalWrite(ledPinGreen, LOW);
	digitalWrite(ledPinYellow, HIGH);
	delay(1000);
}
